# Fritzing sketch ananthakrishnan schematic (saved by Fritzing 0.9.3b)
breadboards: 1

parts:
  Teensy_3_1 = Teensy 3.1
  S1 = Pushbutton [package="[THT]"]
  LED1 = LED - 5mm [color="Red (633nm)" package="5 mm [THT]"]
  R1 = Resistor [tolerance=±5% resistance=220 package=THT]

nets:
  N1: Teensy_3_1.GND, S1.Pin_2, LED1.cathode
  N2: Teensy_3_1.D7, S1.Pin_3, S1.Pin_4
  N3: LED1.anode, R1.Pin_1
